// Digital circuit Demultiplexor 4 a 1.dig as structural Verilog
module Demultiplexor_4_a_1 (
  input  Sel0,
  input  Sel1,
  input  D0,
  output Out1,
  output Out2,
  output Out3,
  output Out4
);

  wire not_1_out, not_2_out;

  not not_1 (not_1_out, Sel0);
  not not_2 (not_2_out, Sel1);
  and and_1 (Out1, D0, Sel1);
  and and_2 (Out2, D0, not_2_out);
  and and_3 (Out3, D0, Sel1);
  and and_4 (Out4, D0, not_2_out);

  // Notes on the sheet:
  //   Como es mencionado, el desmultiplexor es el comportamiento espejo de un multiplexor. 
  //   En base a un multiplexor de 4 entradas, para cumplir las necesidades requeridas, dichas entradas es necesario unirlas
  //   convirtiendolas en una sola entrada. 
  //   Por otro lado, en este caso no se usa la compuerta OR al final, puesto que se busca es obtener cada una de la salidas.
  //   (En este caso, 4 salidas)
endmodule
