// Digital circuit Flip-Flop JK.dig as structural Verilog
module Flip_Flop_JK (
  input  J,
  input  K,
  input  Clock,
  input  clk,
  input  J_2,
  input  K_2,
  output Q,
  output Q_2,
  output Q_3,
  output Q_4
);

  wire nand_1_out, nand_2_out, nand_3_out, nand_4_out, nand_5_out, nand_6_out, not_1_out;

  nand nand_1 (nand_1_out, Q_4, J_2, clk);
  nand nand_2 (nand_2_out, clk, K_2, Q_3);
  JK_FF jk_ff_1 (.J(J), .C(Clock), .K(K), .Q(Q), .nQ(Q_2));
  not not_1 (not_1_out, clk);
  nand nand_3 (nand_3_out, nand_1_out, nand_4_out);
  nand nand_4 (nand_4_out, nand_3_out, nand_2_out);
  nand nand_5 (nand_5_out, not_1_out, nand_3_out);
  nand nand_6 (nand_6_out, nand_4_out, not_1_out);
  nand nand_7 (Q_3, nand_5_out, Q_4);
  nand nand_8 (Q_4, Q_3, nand_6_out);

  // Notes on the sheet:
  //   En esta configuración, al añadir una tercera entrada en las compuertas NAND
  //   y conectarlas directamente a salida, se soluciona el problema que se presentó 
  //   en la configuración RS donde al enecender ambas entradas se ponía en corto.
endmodule
