// Digital circuit Flip-Flop RS.dig as structural Verilog
module Flip_Flop_RS (
  input  S,
  input  R,
  input  S_2,
  input  R_2,
  input  Clock,
  input  Clock_2,
  output Q,
  output Q_2,
  output Q_3,
  output Q_4
);

  wire nand_1_out, nand_2_out, nand_3_out, nand_4_out, nand_5_out, nand_6_out, not_1_out;

  nand nand_1 (nand_1_out, S, Clock);
  nand nand_2 (nand_2_out, Clock, R);
  RS_FF rs_ff_1 (.S(S_2), .C(Clock_2), .R(R_2), .Q(Q), .nQ(Q_2));
  not not_1 (not_1_out, Clock);
  nand nand_3 (nand_3_out, nand_1_out, nand_4_out);
  nand nand_4 (nand_4_out, nand_3_out, nand_2_out);
  nand nand_5 (nand_5_out, not_1_out, nand_3_out);
  nand nand_6 (nand_6_out, nand_4_out, not_1_out);
  nand nand_7 (Q_3, nand_5_out, Q_4);
  nand nand_8 (Q_4, Q_3, nand_6_out);

  // Notes on the sheet:
  //   Esta configuración de Flip-Flop al ser construido con las compuertas lógicas,
  //   se puede notar que al encender R y S a la vez, inmediatamente entra en contro,
  //   pero en ensencia si se miran ambas entradas por separado se puede ver que 
  //   tiene el mismo comportamiento del Flip-Flop RS proporcionado por Digital
endmodule
