// Digital circuit Multiplexor 8 a 1.dig as structural Verilog
module Multiplexor_8_a_1 (
  input  D1,
  input  D2,
  input  D3,
  input  D4,
  input  D5,
  input  D6,
  input  D0,
  input  D7,
  input  S0,
  input  S1,
  input  S2,
  output Out
);

  wire and_1_out, and_2_out, and_3_out, and_4_out, and_5_out, and_6_out, and_7_out, and_8_out, not_1_out,
       not_2_out, not_3_out, or_1_out, or_2_out;

  not not_1 (not_1_out, S0);
  not not_2 (not_2_out, S1);
  not not_3 (not_3_out, S2);
  and and_1 (and_1_out, D0, S0, S1, S2);
  and and_2 (and_2_out, D1, S0, S1, not_3_out);
  and and_3 (and_3_out, D2, S0, not_2_out, S2);
  and and_4 (and_4_out, D3, S0, not_2_out, not_3_out);
  and and_5 (and_5_out, D4, not_1_out, S1, S2);
  and and_6 (and_6_out, D5, not_1_out, S1, not_3_out);
  and and_7 (and_7_out, D6, not_1_out, not_2_out, S2);
  and and_8 (and_8_out, D7, not_1_out, not_2_out, not_3_out);
  or or_1 (or_1_out, and_1_out, and_2_out, and_3_out, and_4_out);
  or or_2 (or_2_out, and_5_out, and_6_out, and_7_out, and_8_out);
  or or_3 (Out, or_1_out, or_2_out);

  // Notes on the sheet:
  //   La tabla de verdad de la compuerta OR se puede ver como una suma,
  //   por esto funciona usar dos compuertas OR de 4 entradas, que sería equivalente a una OR de 8 entradas
  //   donde finalmente se obtendrá una sola salida.
endmodule
