// Digital circuit Pin_Input_Output.dig as structural Verilog
module Pin_Input_Output (
  input  Input0,
  input  Input1,
  input  Input2,
  input  Input3,
  input  Set,
  input  Enable,
  input  Clear,
  input  In0,
  input  In1,
  input  In2,
  input  In3,
  input  Set_2,
  input  Enable_2,
  input  Clear_2,
  input  Set_3,
  input  Enable_3,
  input  Clear_3,
  input  Clock,
  input  Clock_2,
  input  Clock_3,
  input  R0,
  input  R1,
  input  R2,
  input  R3,
  output Out0,
  output Out1,
  output Out2,
  output Out3,
  output out_16,
  output out_17,
  output out_18,
  output out_19
);

  wire d_ff_as_9_q, d_ff_as_10_q, d_ff_as_11_q, d_ff_as_12_q, multiplexer_1_out, multiplexer_2_out,
       multiplexer_3_out, multiplexer_4_out, multiplexer_5_out, multiplexer_6_out, multiplexer_7_out,
       multiplexer_8_out, multiplexer_9_out, multiplexer_10_out, multiplexer_11_out, multiplexer_12_out, S0,
       S1, S2, S3, St0, St1, St2, St3;

  Multiplexer multiplexer_1 (.sel(Enable_3), .in_0(S0), .in_1(R0), .out(multiplexer_1_out));
  PullDown pulldown_1 (.out(St0));
  D_FF_AS d_ff_as_1 (.Set(Set_3), .D(multiplexer_1_out), .C(Clock), .Clr(Clear_3), .Q(S0));  // open: nQ
  Multiplexer multiplexer_2 (.sel(Enable_2), .in_0(out_16), .in_1(St0), .out(multiplexer_2_out));
  D_FF_AS d_ff_as_2 (.Set(Set_2), .D(multiplexer_2_out), .C(Clock_2), .Clr(Clear_2), .Q(out_16));  // open: nQ
  Multiplexer multiplexer_3 (.sel(Enable_3), .in_0(S1), .in_1(R1), .out(multiplexer_3_out));
  PullDown pulldown_2 (.out(St1));
  D_FF_AS d_ff_as_3 (.Set(Set_3), .D(multiplexer_3_out), .C(Clock), .Clr(Clear_3), .Q(S1));  // open: nQ
  Multiplexer multiplexer_4 (.sel(Enable_2), .in_0(out_17), .in_1(St1), .out(multiplexer_4_out));
  D_FF_AS d_ff_as_4 (.Set(Set_2), .D(multiplexer_4_out), .C(Clock_2), .Clr(Clear_2), .Q(out_17));  // open: nQ
  Multiplexer multiplexer_5 (.sel(Enable_3), .in_0(S2), .in_1(R2), .out(multiplexer_5_out));
  PullDown pulldown_3 (.out(St2));
  Multiplexer multiplexer_6 (.sel(Enable_2), .in_0(out_18), .in_1(St2), .out(multiplexer_6_out));
  D_FF_AS d_ff_as_5 (.Set(Set_3), .D(multiplexer_5_out), .C(Clock), .Clr(Clear_3), .Q(S2));  // open: nQ
  D_FF_AS d_ff_as_6 (.Set(Set_2), .D(multiplexer_6_out), .C(Clock_2), .Clr(Clear_2), .Q(out_18));  // open: nQ
  Multiplexer multiplexer_7 (.sel(Enable_3), .in_0(S3), .in_1(R3), .out(multiplexer_7_out));
  PullDown pulldown_4 (.out(St3));
  Multiplexer multiplexer_8 (.sel(Enable_2), .in_0(out_19), .in_1(St3), .out(multiplexer_8_out));
  D_FF_AS d_ff_as_7 (.Set(Set_3), .D(multiplexer_7_out), .C(Clock), .Clr(Clear_3), .Q(S3));  // open: nQ
  D_FF_AS d_ff_as_8 (.Set(Set_2), .D(multiplexer_8_out), .C(Clock_2), .Clr(Clear_2), .Q(out_19));  // open: nQ
  Multiplexer multiplexer_9 (.sel(Enable), .in_0(d_ff_as_9_q), .in_1(Input0), .out(multiplexer_9_out));
  D_FF_AS d_ff_as_9 (.Set(Set), .D(multiplexer_9_out), .C(Clock_3), .Clr(Clear), .Q(d_ff_as_9_q));  // open: nQ
  assign Out0 = ~d_ff_as_9_q ? S0 : 1'bz;  // DriverInvSel driverinvsel_1
  Multiplexer multiplexer_10 (.sel(Enable), .in_0(d_ff_as_10_q), .in_1(Input1), .out(multiplexer_10_out));
  assign St0 = d_ff_as_9_q ? In0 : 1'bz;  // Driver driver_1
  D_FF_AS d_ff_as_10 (.Set(Set), .D(multiplexer_10_out), .C(Clock_3), .Clr(Clear), .Q(d_ff_as_10_q));  // open: nQ
  assign Out1 = ~d_ff_as_10_q ? S1 : 1'bz;  // DriverInvSel driverinvsel_2
  assign St1 = d_ff_as_10_q ? In1 : 1'bz;  // Driver driver_2
  Multiplexer multiplexer_11 (.sel(Enable), .in_0(d_ff_as_11_q), .in_1(Input2), .out(multiplexer_11_out));
  D_FF_AS d_ff_as_11 (.Set(Set), .D(multiplexer_11_out), .C(Clock_3), .Clr(Clear), .Q(d_ff_as_11_q));  // open: nQ
  assign Out2 = ~d_ff_as_11_q ? S2 : 1'bz;  // DriverInvSel driverinvsel_3
  assign St2 = d_ff_as_11_q ? In2 : 1'bz;  // Driver driver_3
  Multiplexer multiplexer_12 (.sel(Enable), .in_0(d_ff_as_12_q), .in_1(Input3), .out(multiplexer_12_out));
  D_FF_AS d_ff_as_12 (.Set(Set), .D(multiplexer_12_out), .C(Clock_3), .Clr(Clear), .Q(d_ff_as_12_q));  // open: nQ
  assign Out3 = ~d_ff_as_12_q ? S3 : 1'bz;  // DriverInvSel driverinvsel_4
  assign St3 = d_ff_as_12_q ? In3 : 1'bz;  // Driver driver_4

  // Notes on the sheet:
  //   Nota: Para el correcto funcionamiento el enable siempre debe estar encendido
  //   Registro con el cual se controla el estado del pin al ser salida.
  //   Registro que almacena el estado del pin con el que fue configurado
  //   Registro de configuración
endmodule
